# Fritzing sketch Bioe3090_Incubator_Schematic (saved by Fritzing 0.9.2b)
breadboards: 1

parts:
  Part1 = Arduino Uno (Rev3)
  Heater = Peltier Element
  Q3 = MOSFET-NCHANNEL [package=to220v]  # not connected
  DS1 = DS18B20 1-Wire Temperature Sensor [part_number=DS18B20]
  Pullup = Resistor [tolerance=±5% resistance=4.7k package="1206 [SMD]"]
  J1 = Power Jack [package=power_jack_combo]
  Pulldown = Resistor [tolerance=±0.1% resistance=10k package=THT]
  DS2 = DS18B20 1-Wire Temperature Sensor [part_number=DS18B20]
  D1 = Rectifier Diode [part_number=1N4001 package="300 mil [THT]"]
  R1 = Resistor [tolerance=±5% resistance=3.3M package=THT]
  R2 = Resistor [tolerance=±5% resistance=2.2M package=THT]
  R3 = Resistor [tolerance=±5% resistance=390 package=THT]
  LED1 = LED - 5mm [color="Red (633nm)" package="5 mm [THT]"]
  F1 = FUSE [package=fuse_5mm]
  C1 = Electrolytic Capacitor [capacitance=1mF package="100 mil [THT, electrolytic]"]
  U1 = SWITCH_SPDT [package=kps-1290]

nets:
  N1: Part1.A0, R1.Pin_0, R2.Pin_1
  GND: Part1.GND, DS1.GND, J1.GND, Pulldown.Pin_0, DS2.GND, R2.Pin_0, R3.Pin_0, C1.+
  N2: Part1.D6_PWM, Pulldown.Pin_1
  N3: Part1.D7, DS1.DQ, Pullup.Pin_1, DS2.DQ
  VDD: Part1.5V, DS1.VDD, Pullup.Pin_0, DS2.VDD
  N4: Heater.pin2, D1.cathode, R1.Pin_1, LED1.anode, C1.-
  N5: J1.GNDBREAK, U1.P
  N6: D1.anode, F1.1
  N7: R3.Pin_1, LED1.cathode
  N8: F1.2, U1.O

notes:
  12V Power from Battery
